// Logisim project flipflooop.circ as structural Verilog: 1 circuit, main circuit main
module main (
  output out_1
);

  wire _1_out, _3_out, _5_out, _6_out, _7_out, _8_out, _9_out, _10_out, _11_out, _13_out, clock_1_out,
       d_ff_1_q, d_ff_1_qn, d_ff_2_q, d_ff_2_qn, d_ff_3_q, d_ff_3_qn, d_ff_4_q, d_ff_4_qn, not_1_out,
       not_2_out, not_3_out, not_4_out, or_1_out, or_2_out, or_3_out, undriven, undriven_2, undriven_3;

  and _0 (out_1, not_1_out, not_2_out, not_3_out, not_4_out);
  Clock clock_1 (.out(clock_1_out));
  and _1 (_1_out, d_ff_1_q, not_2_out, not_3_out, not_4_out);
  // AND_Gate _2 has open pins: in0=not_1_out, in1=d_ff_2_q, in2=not_3_out, in3=not_4_out, out=open
  and _3 (_3_out, d_ff_1_q, d_ff_2_q, not_3_out, not_4_out);
  not not_1 (not_1_out, d_ff_1_q);
  D_Flip_Flop d_ff_1 (.clk(clock_1_out), .D(d_ff_1_qn), .Q(d_ff_1_q), .Qn(d_ff_1_qn));  // open: preset, en, reset
  LED led_1 (.in(undriven_3));
  and _5 (_5_out, d_ff_1_q, not_2_out, d_ff_3_q, not_4_out, undriven);
  // AND_Gate _4 has open pins: in0=not_1_out, in1=not_2_out, in2=d_ff_3_q, in3=not_4_out, out=open
  not not_2 (not_2_out, d_ff_2_q);
  LED led_2 (.in(undriven_3));
  LED led_3 (.in(undriven_3));
  LED led_4 (.in(undriven_2));
  LED led_5 (.in(undriven_3));
  LED led_6 (.in(undriven_2));
  buf or_1 (or_1_out, _5_out);  // OR_Gate
  and _7 (_7_out, d_ff_1_q, d_ff_2_q, d_ff_3_q, not_4_out);
  and _6 (_6_out, undriven, not_1_out, d_ff_2_q, not_4_out, d_ff_1_q);
  D_Flip_Flop d_ff_2 (.clk(d_ff_1_qn), .D(d_ff_2_qn), .Q(d_ff_2_q), .Qn(d_ff_2_qn));  // open: preset, en, reset
  LED led_7 (.in(undriven_3));
  LED led_8 (.in(undriven_3));
  LED led_9 (.in(undriven_2));
  LED led_10 (.in(undriven_3));
  LED led_11 (.in(undriven_2));
  LED led_12 (.in(undriven_2));
  LED led_13 (.in(or_1_out));
  LED led_14 (.in(or_1_out));
  LED led_15 (.in(or_1_out));
  LED led_16 (.in(or_2_out));
  LED led_17 (.in(or_2_out));
  LED led_18 (.in(or_3_out));
  LED led_19 (.in(or_3_out));
  LED led_20 (.in(or_3_out));
  LED led_21 (.in(or_3_out));
  buf or_2 (or_2_out, _3_out);  // OR_Gate
  and _8 (_8_out, not_1_out, not_2_out, not_3_out, d_ff_4_q);
  not not_3 (not_3_out, d_ff_3_q);
  LED led_22 (.in(undriven_3));
  LED led_23 (.in(undriven_3));
  LED led_24 (.in(undriven_2));
  LED led_25 (.in(undriven_2));
  LED led_26 (.in(or_1_out));
  LED led_27 (.in(or_1_out));
  LED led_28 (.in(or_2_out));
  LED led_29 (.in(or_2_out));
  LED led_30 (.in(or_3_out));
  LED led_31 (.in(or_3_out));
  LED led_32 (.in(or_3_out));
  LED led_33 (.in(or_3_out));
  LED led_34 (.in(or_3_out));
  or or_3 (or_3_out, _1_out, _5_out, _3_out, _6_out, _7_out, _8_out, _9_out, _10_out, _11_out, _13_out);
  and _9 (_9_out, d_ff_1_q, not_2_out, not_3_out, d_ff_4_q);
  and _10 (_10_out, not_1_out, d_ff_2_q, not_3_out, d_ff_4_q);
  not not_4 (not_4_out, d_ff_4_q);
  D_Flip_Flop d_ff_3 (.clk(d_ff_2_qn), .D(d_ff_3_qn), .Q(d_ff_3_q), .Qn(d_ff_3_qn));  // open: preset, en, reset
  LED led_35 (.in(undriven_3));
  LED led_36 (.in(undriven_3));
  LED led_37 (.in(undriven_2));
  LED led_38 (.in(undriven_3));
  LED led_39 (.in(undriven_2));
  LED led_40 (.in(undriven_2));
  LED led_41 (.in(or_1_out));
  LED led_42 (.in(or_1_out));
  LED led_43 (.in(or_2_out));
  and _11 (_11_out, d_ff_1_q, d_ff_2_q, not_3_out, d_ff_4_q);
  LED led_44 (.in(undriven_3));
  LED led_45 (.in(undriven_3));
  LED led_46 (.in(undriven_3));
  LED led_47 (.in(undriven_2));
  // AND_Gate _12 has open pins: in0=not_1_out, in1=not_2_out, in2=d_ff_3_q, in3=d_ff_4_q, out=open
  and _13 (_13_out, d_ff_1_q, not_2_out, d_ff_3_q, d_ff_4_q);
  // AND_Gate Disabled is placed but not wired
  // AND_Gate Disabled_2 is placed but not wired
  D_Flip_Flop d_ff_4 (.clk(d_ff_3_qn), .D(d_ff_4_qn), .Q(d_ff_4_q), .Qn(d_ff_4_qn));  // open: preset, en, reset
endmodule
